# Fritzing sketch semiauto-film-developer (saved by Fritzing 0.9.3b)

parts:
  Part1 = Arduino Mega 2560 (Rev3)
  BREAKOUT1 = ULN2003A breakout board
  MOTOR1 = 28BYJ-48 Stepper Motor
  U1 = TMP36 [package=to-92-kit]
  IR1 = TSOP312.., 314.. [package=THT]
  LCD1 = LCD screen
  LCM1602_IIC1 = LCM1602 IIC [part_number="LCM1602 IIC" chip_label="LCM1602 IIC" package="DIP (Dual Inline) [THT]"]
  VCC1 = 4 x AAA Battery Mount  # not connected

nets:
  N1: Part1.A2, U1.VOUT
  N2: Part1.D21/SCL, Part1.SCL, LCM1602_IIC1.SCL
  N3: Part1.D20/SDA, LCM1602_IIC1.SDA
  3V3: Part1.AREF, Part1.3V3, U1.VCC
  GND: Part1.GND, U1.GND, IR1.Vs, LCM1602_IIC1.GND
  N4: Part1.D11_PWM, IR1.GND
  5V: Part1.5V, IR1.Data, LCM1602_IIC1.VCC
  N5: Part1.D46, BREAKOUT1.In_4
  N6: Part1.D48, BREAKOUT1.In_3
  N7: Part1.D50, BREAKOUT1.In_2
  N8: Part1.D52, BREAKOUT1.In_1
  N9: BREAKOUT1.RED_wire, MOTOR1.RED
  N10: BREAKOUT1.ORANGE_wire, MOTOR1.ORANGE
  N11: BREAKOUT1.YELLOW_wire, MOTOR1.YELLOW
  N12: BREAKOUT1.PINK_wire, MOTOR1.PINK
  N13: BREAKOUT1.BLUE_wire, MOTOR1.BLUE
  VSS: LCD1.VSS, LCM1602_IIC1.VSS
  VDD: LCD1.VDD, LCM1602_IIC1.VDD
  N14: LCD1.V0, LCM1602_IIC1.V0
  N15: LCD1.RS, LCM1602_IIC1.RS
  N16: LCD1.R/W, LCM1602_IIC1.RW
  N17: LCD1.E, LCM1602_IIC1.E
  N18: LCD1.DB0, LCM1602_IIC1.D0
  N19: LCD1.DB1, LCM1602_IIC1.D1
  N20: LCD1.DB2, LCM1602_IIC1.D2
  N21: LCD1.DB3, LCM1602_IIC1.D3
  N22: LCD1.DB4, LCM1602_IIC1.D4
  N23: LCD1.DB5, LCM1602_IIC1.D5
  N24: LCD1.DB6, LCM1602_IIC1.D6
  N25: LCD1.DB7, LCM1602_IIC1.D7
  N26: LCD1.LED-, LCM1602_IIC1.A
  N27: LCD1.LED+, LCM1602_IIC1.K
  N28: LCM1602_IIC1.LED_A, LCM1602_IIC1.LED_B

custom parts:
  ULN2003A breakout board: ULN2003A 7-way Darlington Transistor Driver on breakoutboard
  LCD screen: A standard character display, usually with 2x16 characters. Comes in many colors.
  LCM1602 IIC: I2C-Module to use a 1602 or 2004 LCD on with the wire.h libory Serial LCD Modul
